# Fritzing sketch schematic (saved by Fritzing 0.9.3b)
breadboards: 1

parts:
  Power_plug1 = Power plug
  M1 = DC Motor
  Fuse1 = Fuse with Handler [part_number=Htc-15m]
  Q1 = Basic FET N-Channel [package="TO220 [THT]"]
  Part2 = Adafruit SGP30 [part_number="Adafruit #3709"]
  J1 = Piezo Speaker
  U1 = Voltage Regulator - 5V [package="TO220 [THT]"]
  R3 = Resistor [tolerance=±5% resistance=1k package=THT]
  AM1 = AM2320 Humidity and Temperature Sensor [part_number="Adafruit #3721"]
  DS1 = DS18B20 1-Wire Temperature Sensor [part_number=DS18B20]
  Part3 = Arduino Mega 2560 (Rev3)
  LCD2 = LCD screen
  LCM1602_IIC2 = LCM1602 IIC [part_number="LCM1602 IIC" chip_label="LCM1602 IIC" package="DIP (Dual Inline) [THT]"]
  R4 = Resistor [tolerance=±5% resistance=10k package=THT]
  R5 = Resistor [tolerance=±5% resistance=2.2k package=THT]
  R6 = Resistor [tolerance=±5% resistance=1k package=THT]
  Part4 = Bluetooth HC-05 Macho
  U2 = ESP8266 ESP-01 Upgraded WiFi Module [part_number=ESP8266]

nets:
  GND: Power_plug1.GND, Q1.source, Part2.GND, U1.GND, R3.Pin_1, AM1.GND, DS1.GND, Part3.GND, LCM1602_IIC2.GND, R5.Pin_0, Part4.GND, U2.GND
  N1: Power_plug1.VCC, Fuse1.Connector1
  12V: M1.pin_1, Fuse1.Connector2, U1.input_voltage
  N2: M1.pin_2, Q1.drain
  MOTOR: Q1.gate, Part3.D23
  SDA: Part2.SDA, AM1.SDA, Part3.D20/SDA, Part3.SDA, LCM1602_IIC2.SDA
  SCL: Part2.SCL, AM1.SCL, Part3.D21/SCL, Part3.SCL, LCM1602_IIC2.SCL
  3.3V: Part2.VCC, AM1.VDD, Part3.3V3, U2.VCC
  N3: J1.pin1, R3.Pin_0
  SPEAKER: J1.pin2, Part3.D9_PWM
  5V: U1.output_voltage, DS1.VDD, Part3.5V, LCM1602_IIC2.VCC, R4.Pin_0, Part4.VCC
  DS18B20: DS1.DQ, Part3.D2_PWM, R4.Pin_1
  RX1: Part3.D19/RX1, Part4.TXD
  TX1: Part3.D18/TX1, R6.Pin_0
  RX2: Part3.D17_PWM/RX2, U2.TXD
  TX2: Part3.D16_PWM/TX2, U2.RXD
  LCD_VSS: LCD2.VSS, LCM1602_IIC2.VSS
  LCD_VDD: LCD2.VDD, LCM1602_IIC2.VDD
  LCD_V0: LCD2.V0, LCM1602_IIC2.V0
  LCD_RS: LCD2.RS, LCM1602_IIC2.RS
  LCD_RW: LCD2.R/W, LCM1602_IIC2.RW
  LCD_EN: LCD2.E, LCM1602_IIC2.E
  LCD_DB0: LCD2.DB0, LCM1602_IIC2.D0
  LCD_DB1: LCD2.DB1, LCM1602_IIC2.D1
  LCD_DB2: LCD2.DB2, LCM1602_IIC2.D2
  LCD_DB3: LCD2.DB3, LCM1602_IIC2.D3
  LCD_DB4: LCD2.DB4, LCM1602_IIC2.D4
  LCD_DB5: LCD2.DB5, LCM1602_IIC2.D5
  LCD_DB6: LCD2.DB6, LCM1602_IIC2.D6
  LCD_DB7: LCD2.DB7, LCM1602_IIC2.D7
  LCD_LED+: LCD2.LED+, LCM1602_IIC2.A
  LCD_LED-: LCD2.LED-, LCM1602_IIC2.K
  N4: LCM1602_IIC2.LED_A, LCM1602_IIC2.LED_B
  N5: R5.Pin_1, R6.Pin_1, Part4.RXD

custom parts:
  Adafruit SGP30: Breathe easy with the SGP30 Multi-Pixel Gas Sensor, a fully integrated MOX gas sensor. This is a very fine air quality sensor from the sensor experts at Sensirion, with I2C interfacing and fully calibrated output signals with a typical accuracy of 15% within measured values. The SGP combines multiple metal-oxide sensing elements on one chip to provide more detailed air quality signals. This is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
  AM2320 Humidity and Temperature Sensor: AM2320 I2C Humidity and Temperature Sensor
  LCM1602 IIC: I2C-Module to use a 1602 or 2004 LCD on with the wire.h libory Serial LCD Modul
  ESP8266 ESP-01 Upgraded WiFi Module: Upgraded Version ESP-01,all Flash are upgraded to 1M byte.Also support Cloud service remote transmission.
